# Fritzing sketch backpack (saved by Fritzing 0.9.3b)
stripboards: 1

parts:
  J3 = female pin header, 16 pins [form="♀ (female)"]
  J4 = screw terminal, 5 pins
  R5 = Resistor [tolerance=±5% resistance=220 package=THT]
  U2 = 74HC595 [package="DIP16 [THT]"]
  C12 = Capacitor [package=cap-pth-small2]
  Part1 = Arduino Uno (Rev3)
  R9 = Trimmer Potentiometer [maximum_resistance=10kΩ package=THT]

nets:
  GND: J3.pin1, J3.pin5, J3.pin16, J4.pin2, U2.GND, U2.OE, C12.2, Part1.GND, R9.leg2
  VCC: J3.pin2, J4.pin5, R5.Pin_1, U2.MR, U2.VCC, C12.1, Part1.5V, R9.leg1
  N1: J3.pin3, R9.wiper
  N2: J3.pin4, U2.Q7
  N3: J3.pin6, U2.Q6
  N4: J3.pin11, U2.Q4
  N5: J3.pin12, U2.Q3
  N6: J3.pin13, U2.Q2
  N7: J3.pin14, U2.Q1
  N8: J3.pin15, R5.Pin_0
  N9: J4.pin1, U2.DS, Part1.D11_PWM/MOSI
  N10: J4.pin3, U2.ST_CP, Part1.D12/MISO
  N11: J4.pin4, U2.SH_CP, Part1.D13/SCK

notes:
  104

custom parts:
  Capacitor: Capacitor Standard 0603 ceramic capacitor, and 0.1 leaded capacitor.
