# Fritzing sketch example (saved by Fritzing 0.9.3b)
breadboards: 1

parts:
  LCD1 = LCD screen
  U1 = 74HC595 [package="DIP16 [THT]"]
  Part1 = Arduino Uno (Rev3)
  R5 = Trimmer Potentiometer [maximum_resistance=10kΩ package=THT]
  R10 = Resistor [tolerance=±5% resistance=220 package=THT]
  C2 = Capacitor [package=cap-pth-small2]

nets:
  GND: LCD1.VSS, LCD1.R/W, LCD1.LED-, U1.GND, U1.OE, Part1.GND, R5.leg1, C2.2
  VDD: LCD1.VDD, U1.MR, U1.VCC, Part1.5V, R5.leg2, R10.Pin_1, C2.1
  N1: LCD1.V0, R5.wiper
  N2: LCD1.RS, U1.Q1
  N3: LCD1.E, U1.Q3
  N4: LCD1.DB4, U1.Q4
  N5: LCD1.DB5, U1.Q5
  N6: LCD1.DB6, U1.Q6
  N7: LCD1.DB7, U1.Q7
  N8: U1.SH_CP, Part1.D13/SCK
  N9: U1.ST_CP, Part1.D12/MISO
  N10: U1.DS, Part1.D11_PWM/MOSI

notes:
  104

custom parts:
  Capacitor: Capacitor Standard 0603 ceramic capacitor, and 0.1 leaded capacitor.
